# Fritzing sketch ESP-harpe-v0.2 (saved by Fritzing 0.9.3b)
circuit board: 6.5cm x 4cm
breadboards: 1

parts:
  IRLZ44N = MOSFET-NCHANNEL [package=to220v]
  R3 = Resistor [tolerance=±5% resistance=1k package=THT]
  R2 = Resistor [tolerance=±5% resistance=10k package=THT]
  WeMos_D1 = WeMos D1 Mini
  HT7333 = TEMPERATURE-SENSOR [package=to-92]
  HighVol_module = screw terminal, 2 pins
  Rain_D0 = male pin header, 1 pin [form="♂ (male)"]
  Rain_GND = male pin header, 1 pin [form="♂ (male)"]
  Rain_VCC = male pin header, 1 pin [form="♂ (male)"]
  R1 = Resistor [tolerance=±5% resistance=1k package=THT]
  Solar_panel = screw terminal, 2 pins
  TP1 = TP4056 [chip_label=TP4056 package="DIP (Dual Inline) [THT]"]
  BAT+ = male pin header, 1 pin [form="♂ (male)"]
  BAT- = male pin header, 1 pin [form="♂ (male)"]
  part = male pin header, 1 pin [form="♂ (male)"]
  LDR = male pin header, 1 pin [form="♂ (male)"]
  LED = LED - 3mm [color="Red (633nm)" package="3 mm [THT]"]  # not connected

nets:
  N1: IRLZ44N.G, R3.Pin_0, WeMos_D1.D6
  N2: IRLZ44N.D, HighVol_module.pin1
  N3: IRLZ44N.S, R3.Pin_1, R2.Pin_1, WeMos_D1.G, HT7333.GND, Rain_GND.pin1, TP1.pin6
  N4: R2.Pin_0, WeMos_D1.A0, LDR.pin1
  3V3: WeMos_D1.3V3, HT7333.VCC, Rain_VCC.pin1, part.pin1
  N5: WeMos_D1.D0, WeMos_D1.RST
  N6: WeMos_D1.D1, Rain_D0.pin1
  N7: WeMos_D1.D2, R1.Pin_0
  N8: HT7333.ADJ, HighVol_module.pin2, TP1.pin3
  N9: Solar_panel.pin1, TP1.pin2
  N10: Solar_panel.pin2, TP1.pin1
  N11: TP1.pin4, BAT+.pin1
  N12: TP1.pin5, BAT-.pin1

custom parts:
  TP4056: A DIP stand-in part for whatever IC you want. With 6 pins on a 300mil dual inline package (DIP) footprint.
